// Digital circuit lab03.dig as structural Verilog
module lab03 (
  input  [31:0] instruction,
  input  [31:0] A,
  input  [31:0] B,
  output reg__dst,
  output branch,
  output mem__read,
  output mem__to__reg,
  output mem__write,
  output alu__src,
  output reg__write,
  output zero,
  output [31:0] result,
  output [1:0] alu__op
);

  wire [3:0] u_alu_control_alu_control;

  control #(.applicationType("IVERILOG"), .CodeFile("./control.v")) u_control (
    .instr_op(instruction[31:26]), .reg_dst(reg__dst), .branch(branch), .mem_read(mem__read),
    .mem_to_reg(mem__to__reg), .alu_op(alu__op), .mem_write(mem__write), .alu_src(alu__src),
    .reg_write(reg__write));
  alu_control #(.applicationType("IVERILOG"), .CodeFile("./alu_control.v")) u_alu_control (
    .alu_op(alu__op), .funct(instruction[5:0]), .alu_control(u_alu_control_alu_control));
  alu #(.applicationType("IVERILOG"), .CodeFile("./alu.v")) u_alu (
    .alu_control(u_alu_control_alu_control), .A(A), .B(B), .zero(zero), .result(result));

  // Other names for the same wires on the sheet: instr__5__0[5:0] = instruction[5:0]
endmodule

/* Test case Lab 03 Test Bench:
instruction A          B        zero     result     reg\_dst branch mem\_read mem\_to\_reg alu\_op mem\_write alu\_src reg\_write
*/
